# Fritzing sketch test_schematic_arduino (saved by Fritzing 0.6.3b)

parts:
  Arduino1 = Arduino
  DI1 = 7-Segment LED Display [package=THT]
  R1 = Resistor [tolerance=±5% resistance=220 package=THT]
  R2 = Resistor [tolerance=±5% resistance=220 package=THT]
  R3 = Photocell (LDR) [package=THT]
  R4 = Resistor [tolerance=±5% resistance=220 package=THT]

nets:
  N1: Arduino1.D13, R1.Pin_0
  N2: Arduino1.D12, DI1.cathodeE
  N3: Arduino1.D11, DI1.cathodeD
  N4: Arduino1.D10, DI1.cathodeC
  N5: Arduino1.D9, DI1.cathodeDP
  N6: Arduino1.D8, DI1.cathodeB
  N7: Arduino1.D7, DI1.cathodeA
  N8: Arduino1.D6, DI1.cathodeF
  N9: Arduino1.D5, DI1.cathodeG
  N10: Arduino1.D2, Arduino1.+5V, R3.pin_0
  N11: Arduino1.GND, Arduino1.A3, R2.Pin_0
  N12: Arduino1.A4, R4.Pin_1
  N13: Arduino1.A5, R2.Pin_1, R3.pin_1
  N14: DI1.commAnode, R1.Pin_1
