# Fritzing sketch dojoduino (saved by Fritzing 0.8.3b)
breadboards: 1

parts:
  7_Segment1 = 7 Segment Display
  R1 = Resistor [tolerance=±5% resistance=330 package=THT]
  R2 = Resistor [tolerance=±5% resistance=330 package=THT]
  R3 = Resistor [tolerance=±5% resistance=330 package=THT]
  R4 = Resistor [tolerance=±5% resistance=330 package=THT]
  R5 = Resistor [tolerance=±5% resistance=330 package=THT]
  R6 = Resistor [tolerance=±5% resistance=330 package=THT]
  R7 = Resistor [tolerance=±5% resistance=330 package=THT]
  R8 = Resistor [tolerance=±5% resistance=330 package=THT]
  Part1 = Arduino Uno (Rev3)
  RE1 = Rotary Encoder [package=THT]
  S1 = Pushbutton [package="[THT]"]

nets:
  N1: 7_Segment1.Segment_G, R1.Pin_0, R1.Pin_1, Part1.D13/SCK
  N2: 7_Segment1.Segment_F, R2.Pin_0, R2.Pin_1, Part1.ICSP_MISO, Part1.D12/MISO
  N3: 7_Segment1.common_anode, Part1.GND, RE1.EncoderPinB
  N4: 7_Segment1.Segment_E, R3.Pin_0, R3.Pin_1, Part1.ICSP_MOSI, Part1.D11_PWM/MOSI
  N5: 7_Segment1.Segment_D, R4.Pin_0, R4.Pin_1, Part1.D10_PWM/SS
  N6: 7_Segment1.Segment_DP, R8.Pin_0, R8.Pin_1, Part1.D9_PWM
  N7: 7_Segment1.Segment_C, R7.Pin_0, R7.Pin_1, Part1.D8
  N8: 7_Segment1.Segment_B, R6.Pin_0, R6.Pin_1, Part1.D7
  N9: 7_Segment1.Segment_A, R5.Pin_0, R5.Pin_1, Part1.D6_PWM
  N10: Part1.A5/SCL, RE1.EncoderPinC
  N11: Part1.5V, RE1.EncoderPinA
  N12: S1.Pin_1, S1.Pin_2
  N13: S1.Pin_3, S1.Pin_4
